# Fritzing sketch circuitWithoutScreen (saved by Fritzing 0.9.3b)
breadboards: 3

parts:
  Part1 = Arduino Uno (Rev3) - ICSP
  Part2 = Arduino Color LCD Shield  # not connected
  DFRobot_DFPlayer_Mini1 = DFRobot DFPlayer Mini [part_number=DFR0299]
  M1 = DC Motor
  Mod1 = KY-018 Photoresistor Module [package="Breakout board"]
  M2 = fc-51 [package=THT]
  SP1 = SPEAKER [package=pcb_mount_speaker]
  U4 = SWITCH_SPDT [package=kps-1290]
  74HC139N1 = 74HC139N [part_number=74HC139N package="DIP (Dual Inline) [THT]"]
  7_Segment1 = 7-Segment LED Display [package=THT]
  LED2 = smd LED [color="Red (633nm)" package="0603 [SMD]"]
  LED3 = smd LED [color="Red (633nm)" package="0603 [SMD]"]
  R2 = Resistor [tolerance=±5% resistance=220 package="2512 [SMD]"]
  Part5 = Adafruit Analog 2-Axis Joystick [part_number="Adafruit #512"]
  M3 = fc-51 [package=THT]
  S4 = H-Bridge with L298N
  M4 = DC Motor
  S5 = H-Bridge with L298N
  M7 = DC Motor
  M8 = DC Motor
  VCC1 = 4 x AAA Battery Mount
  Part6 = Arduino Uno (Rev3) - ICSP  # not connected
  Part7 = TFT 2.8 inch 320x240 Touch w microSD [part_number=1770]  # not connected
  Part8 = 2.4 Touchscreen TFT Breakout w:MicroSD
  J1 = Piezo Speaker

nets:
  N1: Part1.A1, Part5.YOUT
  N2: Part1.A2, Part5.XOUT
  N3: Part1.A5/SCL, Mod1.Vin
  GND: Part1.GND, Mod1.-, M2.pin2, 74HC139N1.1A, 74HC139N1.1Y2, 74HC139N1.GND, R2.Pin_1, Part5.GND, M3.pin2, S4.GND, S5.GND, VCC1.-, J1.pin1
  N4: Part1.D8, M3.pin1
  N5: Part1.D9_PWM, M2.pin1
  N6: Part1.D10_PWM/SS, 74HC139N1.1Y3
  N7: Part1.D11_PWM/MOSI, LED2.anode, LED3.anode
  N8: Part1.D12/MISO, 74HC139N1.1G_
  N9: Part1.D13/SCK, J1.pin2
  N10: Part1.D2, S4.IN1, S4.IN3
  N11: Part1.D3_PWM, S4.IN2, S4.IN4
  N12: Part1.D4, S5.IN1, S5.IN3
  N13: Part1.D5_PWM, S5.ENA, S5.ENB
  N14: Part1.D6_PWM, S4.ENA, S4.ENB, S4.ENA-5V, S4.ENB-5V
  N15: Part1.D7, S5.IN2, S5.IN4
  VCC: Part1.5V, Mod1.S, M2.pin3, 74HC139N1.1B, 74HC139N1.1Y0, 74HC139N1.1Y1, 74HC139N1.VCC, 7_Segment1.commAnode#2, Part5.VCC, M3.pin3
  VIN: Part1.VIN, S5.5V
  N16: DFRobot_DFPlayer_Mini1.SPK_1, SP1.-
  N17: DFRobot_DFPlayer_Mini1.GND-1, DFRobot_DFPlayer_Mini1.GND-2
  N18: DFRobot_DFPlayer_Mini1.SPK_2, SP1.+
  N19: M1.pin_1, S4.M2-02
  N20: M1.pin_2, S4.M2-01
  N21: U4.O, VCC1.+
  12V: U4.S, S4.12V, S5.12V
  N22: 74HC139N1.2Y3, 7_Segment1.cathodeE
  N23: 74HC139N1.2Y2, 7_Segment1.cathodeD
  N24: 74HC139N1.2Y1, 7_Segment1.cathodeC
  N25: 74HC139N1.2Y0, 7_Segment1.cathodeB
  N26: 74HC139N1.2B, 7_Segment1.cathodeA
  N27: 74HC139N1.2A, 7_Segment1.cathodeG
  N28: 74HC139N1.2G_, 7_Segment1.cathodeF
  N29: LED2.cathode, LED3.cathode, R2.Pin_0
  N30: S4.M1-01, M4.pin_1
  N31: S4.M1-02, M4.pin_2
  N32: S5.M1-01, M7.pin_1
  N33: S5.M1-02, M7.pin_2
  N34: S5.M2-01, M8.pin_2
  N35: S5.M2-02, M8.pin_1
  N36: Part8.C/D, Part8.CLK
  N37: Part8.WR, Part8.WR_DC

custom parts:
  KY-018 Photoresistor Module: KY-018 Photoresistor module, used to measure light intensity. It can determine the presence or absence of light.
  Adafruit Analog 2-Axis Joystick: This mini-kit makes it easy to mount a PSP/Xbox-like thumb joystick to your project. The thumbstick is an analog joystick - more accurate and sensitive than just 'directional' joysticks - with a 'press in to select' button. Since it's analog, you'll need two analog reading pins on your microcontroller to determine X and Y. Having an extra digital input will let you read the switch. The pack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
  H-Bridge with L298N: h-bridge
  TFT 2.8 inch 320x240 Touch w microSD: This TFT display is big (2.8" diagonal) bright (4 white-LED backlight) and colorful! 240x320 pixels with individual RGB pixel control. As a bonus, this display has a resistive touchscreen attached to it already, so you can detect finger presses anywhere on the screen.
  2.4 Touchscreen TFT Breakout w:MicroSD: Add some jazz & pizzazz to your project with a color touchscreen LCD. This TFT display is 2.4" diagonal with a bright (4 white-LED) backlight and it's colorful! 240x320 pixels with individual RGB pixel control, this has way more resolution than a black and white 128x64 display. As a bonus, this display has a resistive touchscreen attached to it already, so you can detect finger presses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
